# Fritzing sketch LCD (saved by Fritzing 0.9.3b)
breadboards: 1

parts:
  LCD1 = LCD screen
  Raspberry_Pi_1 = Raspberry Pi 3 [part_number=RPI-3-V1.2]
  R1 = Resistor [tolerance=±5% resistance=3.3k package=THT]
  R2 = Resistor [tolerance=±5% resistance=470 package=THT]

nets:
  VSS: LCD1.VSS, LCD1.R/W, LCD1.LED-, Raspberry_Pi_1.GND, R1.Pin_0
  VDD: LCD1.VDD, Raspberry_Pi_1.5V, R2.Pin_0
  N1: LCD1.V0, R1.Pin_1
  N2: LCD1.RS, Raspberry_Pi_1.GIPO25
  N3: LCD1.E, Raspberry_Pi_1.GIPO24
  N4: LCD1.DB4, Raspberry_Pi_1.GIPO23
  N5: LCD1.DB5, Raspberry_Pi_1.GIPO17
  N6: LCD1.DB6, Raspberry_Pi_1.GIPO18
  N7: LCD1.DB7, Raspberry_Pi_1.GIPO22
  N8: LCD1.LED+, R2.Pin_1
