# Fritzing sketch smartGarage_Distance (saved by Fritzing 0.9.3b)
breadboards: 1

parts:
  Raspberry_Pi_1 = Raspberry Pi 3 [part_number=RPI-3-V1.2]
  hc-sr1 = hc-sr04
  R5 = Resistor [tolerance=±5% resistance=1k package=THT]
  R6 = Resistor [tolerance=±5% resistance=2.2k package=THT]

nets:
  N1: Raspberry_Pi_1.GIPO11, hc-sr1.Trig
  N2: Raspberry_Pi_1.GIPO20, R5.Pin_1, R6.Pin_0
  5V: Raspberry_Pi_1.5V, hc-sr1.VCC
  N3: hc-sr1.Echo, R5.Pin_0
  N4: hc-sr1.GND, R6.Pin_1
