# Fritzing sketch smartGarage_LED_button (saved by Fritzing 0.9.3b)
breadboards: 1

parts:
  Raspberry_Pi_1 = Raspberry Pi 3 [part_number=RPI-3-V1.2]
  LED_MONITOR_CAR = LED - 5mm [color="Red (633nm)" package="5 mm [THT]"]
  LED_MONITOR_TEMP = LED - 5mm [color="Red (633nm)" package="5 mm [THT]"]
  R3 = Resistor [tolerance=±5% resistance=470 package=THT]
  R4 = Resistor [tolerance=±5% resistance=470 package=THT]
  OVERRIDE_TEMP = Pushbutton [package="[THT]"]
  OVERRIDE_CAR = Pushbutton [package="[THT]"]

nets:
  N1: Raspberry_Pi_1.3v3, Raspberry_Pi_1.GIPO26, Raspberry_Pi_1.GIPO12, OVERRIDE_TEMP.Pin_3, OVERRIDE_TEMP.Pin_4, OVERRIDE_CAR.Pin_3, OVERRIDE_CAR.Pin_4
  N2: Raspberry_Pi_1.GND, R3.Pin_0, R4.Pin_0
  N3: LED_MONITOR_CAR.cathode, R3.Pin_1
  N4: LED_MONITOR_TEMP.cathode, R4.Pin_1
  N5: OVERRIDE_TEMP.Pin_1, OVERRIDE_TEMP.Pin_2
  N6: OVERRIDE_CAR.Pin_1, OVERRIDE_CAR.Pin_2
